// Logisim project brainfuck.circ as structural Verilog: 4 circuits, main circuit main
module main (
);

  wire and_2_out, and_3_out, brainfuck_cpu_1_err, brainfuck_cpu_1_stdin_waiting, clk, clock_1_out, clr_2_out,
       clr_out, comparator_1_eq, d_ff_1_q, d_ff_3_q, d_ff_3_qn, d_ff_4_q, deadlock_out, input_deadlock,
       input_dev_zero, input_keyboard, input_rom, keyboard_out, ndev_zero_out, or_1_out, or_2_out, probe___0,
       probe___1, probe__mem_t, rom_out, stdin_read;
  wire [1:0] bitfinder_1_index;
  wire [3:0] rom_2_data;
  wire [5:0] dbg_skip, dbg_stack_size;
  wire [6:0] bit_extender_2_out, keyboard_2_data;
  wire [7:0] bit_extender_1_out, input_rom_t, multiplexer_3_out, probe__1, probe_mem, ram_1_data,
       register_3_q, register_4_q;
  wire [8:0] input_keyboard_t, multiplexer_1_out;
  wire [23:0] counter_2_q, counter_3_q, probe__instr, probe__mem, register_1_q, register_2_q;
  wire [31:0] counter_1_q;

  LED Program_complete (.in(d_ff_1_q));
  Clock clock_1 (.out(clock_1_out));
  or or_1 (or_1_out, rom_out, keyboard_out, ndev_zero_out, deadlock_out);
  Button deadlock (.out(deadlock_out));
  Button ndev_zero (.out(ndev_zero_out));
  Button keyboard (.out(keyboard_out));
  Button rom (.out(rom_out));
  LED Pending_input (.in(brainfuck_cpu_1_stdin_waiting));
  or or_2 (or_2_out, d_ff_1_q, rom_2_data[3]);
  D_Flip_Flop d_ff_1 (.clk(clock_1_out), .D(or_2_out), .Q(d_ff_1_q));  // open: Qn, preset, en, reset
  ROM #(.addrWidth(24), .dataWidth(4)) rom_2 (.addr(register_1_q), .data(rom_2_data));  // open: sel
  Multiplexer #(.select(2), .width(9), .enable("false")) multiplexer_1 (
    .in0({9{1'b0}}), .in1(9'h100), .in2(input_keyboard_t), .in3({1'b1, input_rom_t}),
    .out(multiplexer_1_out), .sel(bitfinder_1_index));
  radio radio_1 (.btn(deadlock_out), .clk(clk), .any_btn(or_1_out), .enable(input_deadlock), .\default (1'b1));
  radio radio_2 (.btn(ndev_zero_out), .clk(clk), .any_btn(or_1_out), .enable(input_dev_zero));  // open: default
  radio radio_3 (.btn(keyboard_out), .clk(clk), .any_btn(or_1_out), .enable(input_keyboard));  // open: default
  radio radio_4 (.btn(rom_out), .clk(clk), .any_btn(or_1_out), .enable(input_rom));  // open: default
  and and_1 (clk, clock_1_out, ~or_2_out);  // AND_Gate
  LED ERROR (.in(brainfuck_cpu_1_err));
  and and_2 (and_2_out, input_keyboard, clk);
  Keyboard #(.buflen(256)) keyboard_2 (
    .clk(and_2_out), .re(stdin_read), .clr(clr_out), .avail(input_keyboard_t[8]), .data(keyboard_2_data));
  Button clr (.out(clr_out));
  Counter #(.width(32), .max('hffffffff)) counter_1 (
    .count(1'b1), .Q(counter_1_q), .clk(clk));  // open: load, D, carry, clr
  // Probe on counter_1_q
  brainfuck_cpu brainfuck_cpu_1 (
    .instr(rom_2_data[2:0]), .instr_ptr(register_1_q), .mem(multiplexer_3_out), .mem_ptr(register_2_q),
    .stdin(multiplexer_1_out[7:0]), .instr_ptr_2(probe__instr), .mem_ptr_2(probe__mem),
    .writing_mem(probe__mem_t), .set_mem(probe_mem), .stdout_ready(probe___1), .stdout(probe__1),
    .stdin_read(probe___0), .clk(clk), .err(brainfuck_cpu_1_err), .dbg_stack_length(dbg_stack_size),
    .dbg_skip_stack_size(dbg_skip), .stdin_ready(multiplexer_1_out[8]),
    .stdin_waiting(brainfuck_cpu_1_stdin_waiting));
  BitFinder #(.width(4)) bitfinder_1 (
    .in({input_rom, input_keyboard, input_dev_zero, input_deadlock}), .index(bitfinder_1_index));  // open: found
  Register #(.width(24)) register_1 (.D(probe__instr), .Q(register_1_q), .clk(clk));  // open: en, clr
  assign bit_extender_1_out = {{1{1'b0}}, keyboard_2_data};  // Bit_Extender bit_extender_1
  Multiplexer #(.width(8), .enable("false")) multiplexer_2 (
    .in0(bit_extender_1_out), .in1({8{1'b0}}), .out(input_keyboard_t[7:0]), .sel(comparator_1_eq));
  Comparator #(.width(7)) comparator_1 (.a(keyboard_2_data), .b(7'b0001100), .eq(comparator_1_eq));  // open: gt, lt
  D_Flip_Flop d_ff_2 (.clk(clk), .D(probe___0), .Q(stdin_read));  // open: Qn, preset, en, reset
  // Probe on probe__instr
  Register #(.width(24)) register_2 (.D(probe__mem), .Q(register_2_q), .clk(clk));  // open: en, clr
  D_Flip_Flop d_ff_3 (.clk(clk), .D(probe__mem_t), .Q(d_ff_3_q), .Qn(d_ff_3_qn));  // open: preset, en, reset
  Register register_3 (.D(probe_mem), .Q(register_3_q), .clk(clk));  // open: en, clr
  D_Flip_Flop d_ff_4 (.clk(clk), .D(probe___1), .Q(d_ff_4_q));  // open: Qn, preset, en, reset
  Register register_4 (.D(probe__1), .Q(register_4_q), .clk(clk));  // open: en, clr
  // Probe on multiplexer_3_out
  // Probe on probe__mem
  Multiplexer #(.width(8), .enable("false")) multiplexer_3 (
    .in0(register_3_q), .in1(ram_1_data), .out(multiplexer_3_out), .sel(d_ff_3_qn));
  // Probe on probe__mem_t
  Counter #(.width(24), .max('hffffff)) counter_2 (
    .count(stdin_read), .Q(counter_2_q), .clk(and_3_out));  // open: load, D, carry, clr
  and and_3 (and_3_out, input_rom, clk);
  Bit_Extender #(.out_width(7), .\type ("sign")) bit_extender_2 (.in(register_4_q), .out(bit_extender_2_out));
  TTY tty_1 (.data(bit_extender_2_out), .clk(clk), .we(d_ff_4_q), .clr(clr_2_out));
  // Probe on probe_mem
  RAM #(.addrWidth(24), .bus("separate")) ram_1 (
    .addr(register_2_q), .din(register_3_q), .data(ram_1_data), .str(d_ff_3_q), .clk(clk), .ld(1'b1));  // open: sel, clr
  // Probe on counter_3_q
  Counter #(.width(24), .max('hffffff)) counter_3 (
    .count(d_ff_4_q), .Q(counter_3_q), .clk(clk));  // open: load, D, carry, clr
  Button clr_2 (.out(clr_2_out));
  // Probe on probe__1
  // Probe on probe___1
  ROM #(.addrWidth(24)) rom_3 (.addr(counter_2_q), .data(input_rom_t));  // open: sel
  // Probe on probe___0
  RAM #(.addrWidth(24), .bus("separate")) ram_2 (
    .addr(counter_3_q), .din(register_4_q), .str(d_ff_4_q), .clk(clk));  // open: data, sel, ld, clr

  // Notes on the sheet:
  //   contents of rom_2 (hex, n*v repeats v):
  //   4*0 5 6 4*0 5 7 2 6 4*1 7 4*0 6 1 6 3 7 4*0 6 3 7 1 1 1 6 1 1 2 5*0 2 1 1 1 3 7 4*0 6 1 3 4*1 2 5*0
  //   3 7 5*1 6 5*0 2 5*1 3 7 4*0 6 1 1 1 2 0 0 0 6 3 7 7 4*1 2 0 3 6 1 3 0 6 0 2 1 6 3 7 7 7 1 1 6 0 0 2
  //   1 1 3 7 0 1 45*2 6*0 7 2 6 4*1 7 2 6 3 0 0 0 6 1 1 6 49*2 4*1 6 4*0 2 4*1 3 4*1 6 8*0 2 8*1 3 4*1 6
  //   12*0 2 12*1 3 4*1 6 16*0 2 16*1 3 4*1 6 20*0 2 20*1 3 4*1 6 24*0 2 24*1 3 4*1 6 28*0 2 28*1 3 7 4*0
  //   7 4*0 7 4*0 7 4*0 7 4*0 7 4*0 7 4*0 4 6 3 7 7 0 0 0 4 1 3 7 0 7 8
  //   contents of rom_3 (hex, n*v repeats v):
  //   f e f e 5 6 f e f e 5 7 2 6 4*1 7 f e f e 6 1 6 3 7 f e f e 6 3 7 1 1 1 6 1 1 2 f e f e d 2 1 1 1 3
  //   7 f e d d 6 1 3 4*1 2 f e f e d 3 7 5*1 6 f e f e d 2 5*1 3 7 f e f e 6 1 1 1 2 f e d 6 3 7 7 4*1 2
  //   d 3 6 1 3 d 6 d 2 1 6 3 7 7 7 1 1 6 f e 2 1 1 3 7 d 1 45*2 f e f e f e 7 2 6 4*1 7 2 6 3 f e d 6 1 1
  //   6 49*2 4*1 6 f e f e 2 4*1 3 4*1 6 f e d f e f e d 2 8*1 3 4*1 6 f e f e f e f e f e f e 2 12*1 3
  //   4*1 6 f e f e d f e f e f e f e f e d 2 16*1 3 4*1 6 f e f e f e f e f e f e f e f e f e f e 2 20*1
  //   3 4*1 6 f e f e f e d f e f e f e f e f e f e f e f e d 2 24*1 3 4*1 6 f e f e f e f e f e f e f e f
  //   e f e f e f e f e f e f e 2 28*1 3 7 f e f e 7 f e f e 7 f e d d 7 f e f e 7 d f e d 7 f e f e 7 f e
  //   f e 4 6 3 7 7 f e d 4 1 3 7 d 7 8
endmodule

// BF\nCPU
module brainfuck_cpu (
  input  [2:0] instr,
  input  [23:0] instr_ptr,
  input  [7:0] mem,
  input  clk,
  input  [23:0] mem_ptr,
  input  stdin_ready,
  input  [7:0] stdin,
  output [23:0] instr_ptr_2,
  output [23:0] mem_ptr_2,
  output writing_mem,
  output [7:0] set_mem,
  output stdout_ready,
  output [7:0] stdout,
  output stdin_read,
  output stdin_waiting,
  output err,
  output [5:0] dbg_skip_stack_size,
  output [5:0] dbg_stack_length
);

  wire and_1_out, and_2_out, and_3_out, and_4_out, and_5_out, and_7_out, and_8_out, comparator_1_eq,
       err_stack, \input , input_minus, input_plus, input_t_t, input_t_t_t, input_t_t_t_t, input_t_t_t_t_t,
       mem____0_out, nand_1_out, or_1_out, or_2_out, skipping_out;
  wire [5:0] adder_1_out, bit_extender_1_out;
  wire [7:0] adder_2_out, bit_extender_2_out;
  wire [23:0] bit_extender_3_out, multiplexer_1_out, register24stack64_1_tail;

  and and_1 (and_1_out, instr[2], instr[1]);
  Register24Stack64 register24stack64_1 (
    .clk(clk), .push(and_2_out), .insert_data(instr_ptr), .pop(and_3_out), .tail(register24stack64_1_tail),
    .err(err_stack), .length(dbg_stack_length));
  and and_2 (and_2_out, input_t_t_t_t, mem____0_out);
  and and_3 (and_3_out, ~mem____0_out, ~skipping_out, input_t_t_t_t_t);  // AND_Gate
  and and_4 (and_4_out, skipping_out, input_t_t_t_t_t);
  assign bit_extender_1_out = {{5{and_4_out}}, and_4_out};  // Bit_Extender bit_extender_1
  Demultiplexer #(.select(3), .enable("false")) demultiplexer_1 (
    .out0(input_t_t_t), .out1(input_t_t), .out2(input_plus), .out3(input_minus), .out4(stdout_ready),
    .out5(\input ), .out6(input_t_t_t_t), .out7(input_t_t_t_t_t), .in(or_1_out), .sel(instr));
  or or_1 (or_1_out, ~skipping_out, and_1_out);  // OR_Gate
  or or_2 (or_2_out, ~mem____0_out, skipping_out);  // OR_Gate
  and and_5 (and_5_out, or_2_out, input_t_t_t_t);
  Adder #(.width(6)) adder_1 (
    .a(bit_extender_1_out), .b(dbg_skip_stack_size), .out(adder_1_out), .cin(and_5_out));  // open: cout
  or mem____0 (mem____0_out, mem[0], mem[1], mem[2], mem[3], mem[4], mem[5], mem[6], mem[7]);
  or skipping (skipping_out, dbg_skip_stack_size[5], dbg_skip_stack_size[4], dbg_skip_stack_size[3], dbg_skip_stack_size[2], dbg_skip_stack_size[1], dbg_skip_stack_size[0]);
  Register #(.width(6)) register_1 (.D(adder_1_out), .Q(dbg_skip_stack_size), .clk(clk));  // open: en, clr
  and and_6 (stdin_read, stdin_ready, \input );
  and and_7 (and_7_out, input_t_t_t_t_t, mem____0_out);
  Multiplexer #(.width(24), .enable("false")) multiplexer_1 (
    .in0(instr_ptr), .in1(register24stack64_1_tail), .out(multiplexer_1_out), .sel(and_7_out));
  assign bit_extender_2_out = {{7{input_minus}}, input_minus};  // Bit_Extender bit_extender_2
  Comparator #(.width(6)) comparator_1 (.a(dbg_stack_length), .b({6{1'b0}}), .eq(comparator_1_eq));  // open: gt, lt
  assign bit_extender_3_out = {{23{input_t_t}}, input_t_t};  // Bit_Extender bit_extender_3
  Adder adder_2 (.a(mem), .b(bit_extender_2_out), .out(adder_2_out), .cin(input_plus));  // open: cout
  and and_8 (and_8_out, comparator_1_eq, input_t_t_t_t_t);
  nand nand_1 (nand_1_out, ~stdin_ready, \input );  // NAND_Gate
  Adder #(.width(24)) adder_3 (
    .a(multiplexer_1_out), .b({24{1'b0}}), .out(instr_ptr_2), .cin(nand_1_out));  // open: cout
  Adder #(.width(24)) adder_4 (.a(mem_ptr), .b(bit_extender_3_out), .out(mem_ptr_2), .cin(input_t_t_t));  // open: cout
  or or_3 (writing_mem, input_plus, input_minus, stdin_read);
  Multiplexer #(.width(8), .enable("false")) multiplexer_2 (
    .in0(adder_2_out), .in1(stdin), .out(set_mem), .sel(stdin_read));
  and and_9 (stdin_waiting, ~stdin_ready, \input );  // AND_Gate
  or or_4 (err, err_stack, and_8_out);

  assign stdout = mem;

  // Other names for the same wires on the sheet: input_t = stdout_ready; stack_length[5:0] = dbg_stack_length
endmodule

// Register24\nStack[64]
module Register24Stack64 (
  input  clk,
  input  push,
  input  pop,
  input  [23:0] insert_data,
  output [5:0] length,
  output [23:0] tail,
  output err
);

  wire and_1_out, and_2_out, and_3_out, comparator_1_eq, comparator_2_eq, not_1_out, not_2_out, not_3_out,
       or_1_out;
  wire [5:0] adder_1_out, bit_extender_1_out, subtractor_1_out;
  wire [23:0] multiplexer_1_out;

  not not_1 (not_1_out, push);
  Subtractor #(.width(6)) subtractor_1 (
    .a(length), .b({6{1'b0}}), .out(subtractor_1_out), .bin(not_1_out));  // open: bout
  Multiplexer #(.width(24), .enable("false")) multiplexer_1 (
    .in0({24{1'b0}}), .in1(insert_data), .out(multiplexer_1_out), .sel(push));
  assign bit_extender_1_out = {{5{pop}}, pop};  // Bit_Extender bit_extender_1
  not not_2 (not_2_out, err);
  or or_1 (or_1_out, push, pop);
  not not_3 (not_3_out, or_1_out);
  Register #(.width(6)) u_length (.D(adder_1_out), .Q(length), .clk(clk));  // open: en, clr
  Adder #(.width(6)) adder_1 (.a(length), .b(bit_extender_1_out), .out(adder_1_out), .cin(push));  // open: cout
  RAM #(.addrWidth(6), .dataWidth(24), .bus("separate")) ram_1 (
    .addr(subtractor_1_out), .din(multiplexer_1_out), .data(tail), .str(or_1_out), .sel(not_2_out),
    .clk(clk), .ld(not_3_out));  // open: clr
  Comparator #(.width(6)) comparator_1 (.a({6{1'b1}}), .b(length), .eq(comparator_1_eq));  // open: gt, lt
  Comparator #(.width(6)) comparator_2 (.a({6{1'b0}}), .b(length), .eq(comparator_2_eq));  // open: gt, lt
  and and_1 (and_1_out, comparator_1_eq, push);
  and and_2 (and_2_out, push, pop);
  and and_3 (and_3_out, comparator_2_eq, pop);
  or or_2 (err, and_1_out, and_2_out, and_3_out);
endmodule

module radio (
  input  btn,
  input  clk,
  input  any_btn,
  input  \default ,
  output enable
);

  wire and_1_out, and_2_out, d_ff_1_qn;

  S_R_Flip_Flop s_r_ff_1 (.S(btn), .clk(clk), .R(and_1_out), .Q(enable), .preset(and_2_out));  // open: Qn, reset, en
  and and_1 (and_1_out, ~btn, any_btn);  // AND_Gate
  and and_2 (and_2_out, d_ff_1_qn, \default );
  D_Flip_Flop d_ff_1 (.clk(clk), .D(1'b1), .Qn(d_ff_1_qn));  // open: Q, preset, en, reset

  // Notes on the sheet:
  //   default: pull=down
endmodule
